// Digital circuit adder.dig as structural Verilog
module adder (
  input  [7:0] a,
  input  [7:0] b,
  output [7:0] sum,
  output carry
);

  eight_bit_adder #(.applicationType("GHDL"), .CodeFile("\\home\\aluno\\Documentos\\bs\\CC-UFFS\\third-semester\\DIGITALSYSTEMS\\VHDL\\adder\\adder.vhdl")) u_eight_bit_adder (
    .a(a), .b(b), .carry(carry), .sum(sum));
endmodule
