// Digital circuit project.dig as structural Verilog
module project (
  input  [2:0] status_windows,
  input  [1:0] status_door,
  input  secure_mode,
  input  daylight_sensor,
  input  weather_sensor,
  input  max_tank_b
);

  smart_house #(.applicationType("GHDL"), .CodeFile("/home/aluno/Documentos/bs/cc-uffs/third-semester/DIGITALSYSTEMS/assignment1/main.vhdl")) u_smart_house (
    .status_window(status_windows), .status_door(status_door), .secure_mode(secure_mode),
    .daylight_sensor(daylight_sensor), .weather_sensor(weather_sensor), .max_tankB(max_tank_b));  // open: security_alert, window_open_alert, wdopen_rain_alert, wopen_night_alert, wopen_lowtemp_alert, water_pump, eletrovalve
endmodule
